# Fritzing sketch VuMeter (saved by Fritzing 1.0.2b)
breadboards: 1

parts:
  Componente1 = Arduino Pro Mini (3.3V)
  R1 = Rotary Potentiometer (Large) [maximum_resistance=100kΩ knob_status=50% power=0.5W package=THT]
  RCA1 = RCA [package=pth]
  RCA2 = RCA [package=pth]
  R2 = Rotary Potentiometer (Large) [maximum_resistance=100kΩ knob_status=50% power=0.5W package=THT]
  C1 = Film/Foil Capacitor [capacitance=100nF voltage=35V package="7.5mm [THT, pp]"]
  C2 = Film/Foil Capacitor [capacitance=100nF voltage=35V package="7.5mm [THT, pp]"]
  R3 = Resistor [tolerance=±5% power=0.25W resistance=100k package=THT]
  R4 = Resistor [tolerance=±5% power=0.25W resistance=100k package=THT]
  R5 = Resistor [tolerance=±5% power=0.25W resistance=100k package=THT]
  R6 = Resistor [tolerance=±5% power=0.25W resistance=100k package=THT]
  S1 = Momentary Switch [package=ksa_sealed_tac_switch]
  S2 = Momentary Switch [package=ksa_sealed_tac_switch]
  LED1 = smd LED [color="Red (660nm)" package="1206 [SMD]"]
  LED2 = smd LED [color="Yellow (595nm)" package="1206 [SMD]"]
  R7 = Resistor [tolerance=±5% power=0.25W resistance=220 package=THT]
  R8 = Resistor [tolerance=±5% power=0.25W resistance=220 package=THT]
  R9 = Resistor [tolerance=±5% power=0.25W resistance=10k package=THT]
  R10 = Resistor [tolerance=±5% power=0.25W resistance=10k package=THT]
  U1 = Hirose DF13 Series Header [part_number=DF13#-3P-1.25V package=DF13C-3P-1.25V]

nets:
  N1: Componente1.GND, R1.leg2, RCA1.SHELL, RCA2.SHELL, R2.leg2, R4.Pin_1, R6.Pin_1, LED1.cathode, LED2.cathode, R9.Pin_1, R10.Pin_1, U1.3
  N2: R1.leg1, RCA2.PIN
  N3: R1.wiper, C1.+
  N4: RCA1.PIN, R2.leg1
  N5: R2.wiper, C2.+
  N6: C1.-, R3.Pin_1, R4.Pin_0
  N7: C2.-, R5.Pin_1, R6.Pin_0
  N8: R3.Pin_0, R5.Pin_0, S1.3, S2.3, U1.1
  N9: S1.2, R10.Pin_0
  N10: S2.2, R9.Pin_0
  N11: LED1.anode, R7.Pin_0
  N12: LED2.anode, R8.Pin_0

notes:
  SX DX
  dimmer
  mode
  Mode
  1 2
